# Fritzing sketch Circuit - Motors, Steppers and servos (saved by Fritzing 0.9.3b)
circuit board: 8.46667cm x 5.64444cm
breadboards: 1

parts:
  M1 = Stepper Motor - Bipolar
  Pololu_A1 = Pololu A4988 [package=SO16]
  Part1 = Arduino Nano (Rev3.0)
  J1 = Basic Servo
  U1 = POT [package=pot_mammoth]
  LED1 = smd LED [color="Red (633nm)" package="0805 [SMD]"]
  R1 = Resistor [tolerance=±5% resistance=220 package=THT]
  C1 = Electrolytic Capacitor [capacitance=100μF package="0807 [SMD, electrolytic]"]
  VCC1 = Battery block 9V

nets:
  N1: M1.A, Pololu_A1.2B
  N2: M1.C, Pololu_A1.2A
  N3: M1.B, Pololu_A1.1A
  N4: M1.D, Pololu_A1.1B
  N5: Pololu_A1.RESET, Pololu_A1.SLEEP
  N6: Pololu_A1.STEP, Part1.D3
  N7: Pololu_A1.DIR, Part1.D4
  GND: Pololu_A1.GND#8, Part1.GND, J1.gnd, U1.S, LED1.cathode
  VDD: Pololu_A1.VDD, Part1.5V, J1.vcc, U1.E
  N8: Pololu_A1.GND#14, C1.-, VCC1.-
  N9: Pololu_A1.VMOT, C1.+, VCC1.+
  N10: Part1.D8, J1.pulse
  N11: Part1.D9, R1.Pin_1
  N12: Part1.A0, U1.A
  N13: LED1.anode, R1.Pin_0
