# Fritzing sketch Module 4 - LCD RTC Fritzing Sketch (saved by Fritzing 0.9.3b)
breadboards: 1

parts:
  Part2 = Arduino Nano (Rev3.0)
  Part12 = Real Time Clock Module - DS1307 RTC Breakout Board
  LCD1 = LCD screen
  U1 = POT [package=pot_mammoth]
  R1 = Resistor [tolerance=±5% resistance=220 package="2512 [SMD]"]
  R2 = Trimmer Potentiometer [maximum_resistance=10kΩ package=THT]  # not connected
  J1 = Piezo Speaker  # not connected

nets:
  GND: Part2.GND, Part12.GND, U1.S
  N1: Part2.D2, Part12.SQW
  N2: Part2.D3, Part12.SCL
  N3: Part2.D4, Part12.SDA
  N4: Part2.D6, LCD1.RS
  N5: Part2.D7, LCD1.E
  N6: Part2.D8, LCD1.DB4
  N7: Part2.D9, LCD1.DB5
  N8: Part2.D10, LCD1.DB6
  N9: Part2.D11/MOSI, LCD1.DB7
  5V: Part2.5V, Part12.5V, U1.E
  N10: LCD1.VSS, LCD1.R/W, LCD1.LED-
  N11: LCD1.VDD, R1.Pin_0
  N12: LCD1.V0, U1.A
  N13: LCD1.LED+, R1.Pin_1

notes:
  this clock module is different to ours!
