# Fritzing sketch Module 5 - PushButtons and LEDs (saved by Fritzing 0.9.3b)
breadboards: 1

parts:
  Part2 = Arduino Nano (Rev3.0)
  R1 = Resistor [tolerance=±5% resistance=10k package="2512 [SMD]"]
  S1 = Momentary Switch [package=ksa_sealed_tac_switch]
  R2 = Resistor [tolerance=±5% resistance=10k package="2512 [SMD]"]
  S2 = Momentary Switch [package=ksa_sealed_tac_switch]
  LED1 = smd LED [color="Red (633nm)" package="0805 [SMD]"]
  LED2 = smd LED [color="Red (633nm)" package="0805 [SMD]"]
  LED3 = smd LED [color="Red (633nm)" package="0805 [SMD]"]
  R3 = Resistor [tolerance=±5% resistance=10k package="2512 [SMD]"]
  R4 = Resistor [tolerance=±5% resistance=10k package="2512 [SMD]"]
  R5 = Resistor [tolerance=±5% resistance=10k package="2512 [SMD]"]

nets:
  N1: Part2.GND, R1.Pin_1, R3.Pin_1
  N2: Part2.D2, S1.1
  N3: Part2.D3, S2.1
  N4: Part2.D4, LED2.anode
  N5: Part2.D5, LED1.anode
  N6: Part2.D6, LED3.anode
  N7: R1.Pin_0, S1.2
  N8: R2.Pin_0, S2.2
  N9: R2.Pin_1, R4.Pin_1, R5.Pin_1
  N10: LED1.cathode, R3.Pin_0
  N11: LED2.cathode, R4.Pin_0
  N12: LED3.cathode, R5.Pin_0

notes:
  Button 1 LED
  Button 2 LED
  Result LED
